// Logisim project hrmcpu.circ as structural Verilog: 9 circuits, main circuit top
module top (
);

  wire alu_1_flag, branch, ControlUnit_p1, empty, fb, full, ijump, muxM, rIN, rst, rstPC, srcA, undriven,
       wIR, wM, wO, wPC, wR;
  wire [1:0] muxR;
  wire [2:0] aluCtl;
  wire [7:0] alu_1_aluout, inbox_1_din, INSTR, memory_1_m, pc_1_pc, r_1_r;

  // Probe on inbox_1_din
  INBOX inbox_1 (.rIn(rIN), .rst(rst), .empty(empty), .DIN(inbox_1_din));
  // Probe on r_1_r
  R r_1 (.iInbox(inbox_1_din), .iMem(memory_1_m), .iAlu(alu_1_aluout), .muxR(muxR), .wR(wR), .R(r_1_r));
  // Probe on memory_1_m
  MEMORY memory_1 (
    .PC(pc_1_pc), .srcA(srcA), .wM(wM), .R(r_1_r), .aluOut(alu_1_aluout), .muxM(muxM), .fb(fb), .M(memory_1_m));
  // Probe on INSTR
  IR ir_1 (.nIR(memory_1_m), .wIR(wIR), .rIR(INSTR));
  // Probe on pc_1_pc
  PC pc_1 (
    .branch(branch), .ijump(ijump), .aluFlag(alu_1_flag), .jmpAddr(memory_1_m), .wPC(wPC), .rst(rstPC),
    .PC(pc_1_pc));
  ALU alu_1 (.inR(r_1_r), .inM(memory_1_m), .aluCtl(aluCtl), .flag(alu_1_flag), .aluOut(alu_1_aluout));
  // FSM_Entity #(.content("fsm ControlUnit @[ 34 , 30 , 1200 , 800 ]\n{ in INSTR [ 8 ] @[ 34 , 100 , 72 , 15 ]\n;\nin inEmpty [ 1 ] @[ 34 , 140 , 56 , 15 ]\n;\nin outFull [ 1 ] @[ 34 , 178 , 47 , 15 ]\n;\nout wIR [ 1 ] @[ 1207 , 93 , 27 , 15 ]\n;\nout muxR [ 2 ] @[ 1165 , 150 , 69 , 15 ]\n;\nout wR [ 1 ] @[ 1210 , 177 , 24 , 15 ]\n;\nout muxM [ 1 ] @[ 1191 , 222 , 43 , 15 ]\n;\nout srcA [ 1 ] @[ 1200 , 244 , 34 , 15 ]\n;\nout wM [ 1 ] @[ 1208 , 268 , 26 , 15 ]\n;\nout fb [ 1 ] @[ 1216 , 303 , 18 , 15 ]\n;\nout aluCtl [ 3 ] @[ 1164 , 333 , 70 , 15 ]\n;\nout wPC [ 1 ] @[ 1201 , 366 , 33 , 15 ]\n;\nout rIn [ 1 ] @[ 1211 , 390 , 23 , 15 ]\n;\nout wO [ 1 ] @[ 1208 , 415 , 26 , 15 ]\n;\nout ijump [ 1 ] @[ 1194 , 467 , 40 , 15 ]\n;\nout branch [ 1 ] @[ 1185 , 490 , 49 , 15 ]\n;\nout rst [ 1 ] @[ 1210 , 523 , 24 , 15 ]\n;\nout halt [ 1 ] @[ 1205 , 553 , 29 , 15 ]\n;\ncodeWidth = 6 ; reset = RESET ; state RESET = \"000000\" @[ 164 , 91 , 30 , 30 ]\n{\ncommands @[ 209 , 106 , 55 , 21 ]\n{\nrst = \"1\" ;\n}\ntransitions {\nRESET -> FETCH1 when default @[ 293 , 74 , 49 , 21 ]\n;\n}\n}\nstate INCRPC = \"000010\" @[ 172 , 171 , 30 , 30 ]\n{\ncommands @[ 217 , 186 , 64 , 21 ]\n{\nwPC = \"1\" ;\n}\ntransitions {\nINCRPC -> FETCH1 when default @[ 255 , 144 , 49 , 21 ]\n;\n}\n}\nstate FETCH1 = \"000100\" @[ 361 , 79 , 30 , 30 ]\n{\ncommands @[ 418 , 89 , 65 , 21 ]\n{\nsrcA = \"1\" ;\n}\ntransitions {\nFETCH1 -> FETCH2 when default @[ 324 , 154 , 49 , 21 ]\n;\n}\n}\nstate FETCH2 = \"000110\" @[ 296 , 193 , 30 , 30 ]\n{\ncommands @[ 341 , 208 , 58 , 21 ]\n{\nwIR = \"1\" ;\n}\ntransitions {\nFETCH2 -> DECODE when default @[ 255 , 260 , 49 , 21 ]\n;\n}\n}\nstate INBOX1 = \"001000\" @[ 166 , 430 , 30 , 30 ]\n{\ncommands @[ 212 , 445 , 54 , 21 ]\n{\nrIn = \"1\" ;\n}\ntransitions {\nINBOX1 -> INBOX2 when default @[ 153 , 495 , 49 , 21 ]\n;\n}\n}\nstate INBOX2 = \"001010\" @[ 159 , 527 , 30 , 30 ]\n{\ncommands @[ 205 , 542 , 79 , 36 ]\n{\nmuxR = \"00\" ;\nwR = \"1\" ;\n}\ntransitions {\nINBOX2 -> INCRPC when default @[ 37 , 448 , 49 , 21 ]\n;\n}\n}\nstate OUTBOX = \"001100\" @[ 282 , 436 , 30 , 30 ]\n{\ncommands @[ 327 , 451 , 57 , 21 ]\n{\nwO = \"1\" ;\n}\ntransitions {\nOUTBOX -> INCRPC when default @[ 165 , 343 , 49 , 21 ]\n;\n}\n}\nstate INCPC2 = \"001110\" @[ 393 , 415 , 30 , 30 ]\n{\ncommands @[ 439 , 430 , 64 , 21 ]\n{\nwPC = \"1\" ;\n}\ntransitions {\nINCPC2 -> FETCH3 when default @[ 408 , 467 , 49 , 21 ]\n;\n}\n}\nstate FETCH3 = \"010000\" @[ 393 , 500 , 30 , 30 ]\n{\ncommands @[ 450 , 513 , 65 , 21 ]\n{\nsrcA = \"1\" ;\n}\ntransitions {\nFETCH3 -> READMEM when default @[ 405 , 554 , 49 , 21 ]\n;\n}\n}\nstate READMEM = \"010010\" @[ 397 , 582 , 30 , 30 ]\n{\ncommands @[ 457 , 597 , 49 , 21 ]\n{\nfb = \"1\" ;\n}\ntransitions {\nREADMEM -> WAIT1 when default @[ 406 , 640 , 49 , 21 ]\n;\nREADMEM -> COPYTO when INSTR [ 7 : 4 ] == \"0011\" @[ 492 , 664 , 143 , 21 ]\n;\n}\n}\nstate COPYFROM = \"010100\" @[ 398 , 723 , 30 , 30 ]\n{\ncommands @[ 443 , 738 , 79 , 36 ]\n{\nmuxR = \"01\" ;\nwR = \"1\" ;\n}\ntransitions {\nCOPYFROM -> INCRPC when default @[ 85 , 624 , 49 , 21 ]\n;\n}\n}\nstate DECODE = \"010110\" @[ 268 , 288 , 30 , 30 ]\n{\ncommands @[ 313 , 303 , 30 , 20 ]\n{\n}\ntransitions {\nDECODE -> INCPC2 when INSTR [ 7 : 4 ] == \"0010\" @[ 341 , 327 , 143 , 21 ]\n;\nDECODE -> OUTBOX when INSTR [ 7 : 4 ] == \"0001\" @[ 244 , 388 , 143 , 21 ]\n;\nDECODE -> INBOX1 when INSTR [ 7 : 4 ] == \"0000\" @[ 169 , 367 , 143 , 21 ]\n;\nDECODE -> INCRPC when default @[ 203 , 267 , 49 , 21 ]\n;\nDECODE -> HALT1 when INSTR [ 7 : 4 ] == \"1111\" @[ 303 , 411 , 143 , 21 ]\n;\nDECODE -> INCPC2 when INSTR [ 7 : 4 ] == \"0011\" @[ 353 , 302 , 143 , 21 ]\n;\n}\n}\nstate HALT1 = \"011000\" @[ 281 , 566 , 30 , 30 ]\n{\ncommands @[ 326 , 580 , 60 , 21 ]\n{\nhalt = \"1\" ;\n}\ntransitions {\nHALT1 -> HALT2 when default @[ 310 , 632 , 49 , 21 ]\n;\n}\n}\nstate HALT2 = \"011010\" @[ 280 , 656 , 30 , 30 ]\n{\ncommands @[ 325 , 670 , 60 , 21 ]\n{\nhalt = \"1\" ;\n}\ntransitions {\nHALT2 -> HALT1 when default @[ 250 , 634 , 49 , 21 ]\n;\n}\n}\nstate WAIT1 = \"011100\" @[ 397 , 651 , 30 , 30 ]\n{\ncommands @[ 442 , 666 , 30 , 20 ]\n{\n}\ntransitions {\nWAIT1 -> COPYFROM when default @[ 406 , 712 , 49 , 21 ]\n;\n}\n}\nstate COPYTO = \"011110\" @[ 527 , 767 , 30 , 30 ]\n{\ncommands @[ 572 , 782 , 57 , 21 ]\n{\nwM = \"1\" ;\n}\ntransitions {\nCOPYTO -> INCRPC when default @[ 65 , 679 , 49 , 21 ]\n;\n}\n}\n}")) ControlUnit: pin names not known; wires that end beside it: ControlUnit_p1, rst, 1'b1, INSTR, empty, full, wIR, muxR, wR, muxM, srcA, wM, fb, aluCtl, wPC, rIN, wO, ijump
  Clock clock_1 (.out(ControlUnit_p1));
  OUTBOX outbox_1 (.DOUT(r_1_r), .wO(wO), .full(full));
  Button rstBtn (.out(rst));
  LED Halt (.in(undriven));
endmodule

module PC (
  input  branch,
  input  ijump,
  input  aluFlag,
  input  [7:0] jmpAddr,
  input  wPC,
  input  rst,
  output [7:0] PC
);

  wire and_1_out, clock_1_out, or_1_out, or_2_out;
  wire [7:0] adder_1_out, multiplexer_1_out, multiplexer_2_out;

  or or_1 (or_1_out, ijump, aluFlag);
  and and_1 (and_1_out, branch, or_1_out);
  Multiplexer #(.width(8), .enable("false")) multiplexer_1 (
    .in0(adder_1_out), .in1(jmpAddr), .out(multiplexer_1_out), .sel(and_1_out));
  Multiplexer #(.width(8), .enable("false")) multiplexer_2 (
    .in0(multiplexer_1_out), .in1(8'h20), .out(multiplexer_2_out), .sel(rst));
  // Probe on multiplexer_2_out
  or or_2 (or_2_out, rst, wPC);
  Register rPC (.D(multiplexer_2_out), .en(or_2_out), .clk(clock_1_out), .Q(PC));  // open: clr
  Clock clock_1 (.out(clock_1_out));
  // Probe on adder_1_out
  Adder adder_1 (.a(PC), .b(8'h1), .out(adder_1_out));  // open: cin, cout
endmodule

module INBOX (
  input  rIn,
  input  rst,
  output empty,
  output [7:0] DIN
);

  wire clock_1_out, clock_2_out;
  wire [7:0] adder_1_out, inCursor_q, undriven;

  Clock clock_1 (.out(clock_1_out));
  Register inCursor (.D(adder_1_out), .en(rIn), .clk(clock_1_out), .Q(inCursor_q), .clr(rst));
  ROM rom_1 (.addr(inCursor_q));  // open: data
  Adder adder_1 (.a(inCursor_q), .b(8'h1), .out(adder_1_out));  // open: cin, cout
  Comparator comparator_1 (.a(inCursor_q), .b(8'hf), .eq(empty));  // open: gt, lt
  Register inboxData (.D(undriven), .en(1'b1), .clk(clock_2_out), .Q(DIN), .clr(rst));
  Clock clock_2 (.out(clock_2_out));

  // Notes on the sheet:
  //   contents of rom_1 (hex, n*v repeats v):
  //   f0 f1
endmodule

module IR (
  input  [7:0] nIR,
  input  wIR,
  output [7:0] rIR
);

  wire clock_1_out;

  Register register_1 (.D(nIR), .en(wIR), .clk(clock_1_out), .Q(rIR));  // open: clr
  Clock clock_1 (.out(clock_1_out));
endmodule

module R (
  input  [7:0] iInbox,
  input  [7:0] iMem,
  input  [7:0] iAlu,
  input  [1:0] muxR,
  input  wR,
  output [7:0] R
);

  wire clock_1_out;
  wire [7:0] multiplexer_1_out;

  Multiplexer #(.select(2), .width(8), .enable("false")) multiplexer_1 (
    .in0(iInbox), .in1(iMem), .in3(iAlu), .out(multiplexer_1_out), .sel(muxR));  // open: in2
  Register register_1 (.D(multiplexer_1_out), .en(wR), .clk(clock_1_out), .Q(R));  // open: clr
  Clock clock_1 (.out(clock_1_out));
endmodule

module MEMORY (
  input  [7:0] PC,
  input  srcA,
  input  wM,
  input  [7:0] R,
  input  [7:0] aluOut,
  input  muxM,
  input  fb,
  output [7:0] M
);

  wire clock_1_out, clock_2_out;
  wire [7:0] indirectFeedback_q, multiplexer_1_out, multiplexer_2_out;

  Register indirectFeedback (.D(M), .en(fb), .clk(clock_1_out), .Q(indirectFeedback_q));  // open: clr
  Clock clock_1 (.out(clock_1_out));
  Multiplexer #(.width(8), .enable("false")) multiplexer_1 (
    .in0(indirectFeedback_q), .in1(PC), .out(multiplexer_1_out), .sel(srcA));
  Clock clock_2 (.out(clock_2_out));
  Multiplexer #(.width(8), .enable("false")) multiplexer_2 (.in0(R), .in1(aluOut), .out(multiplexer_2_out), .sel(muxM));
  // Probe on multiplexer_1_out
  // RAM #(.databus("bibus")) ram_1: pin names not known; wires that end beside it: multiplexer_1_out, wM

  // Notes on the sheet:
  //   Select Value Input
  //   contents of ram_1 (hex, n*v repeats v):
  //   f0 32*0 30 0 0 10 20 0 10 f0 20 1
endmodule

module ALU (
  input  [7:0] inR,
  input  [7:0] inM,
  input  [2:0] aluCtl,
  output flag,
  output [7:0] aluOut
);
endmodule

module OUTBOX (
  input  [7:0] DOUT,
  input  wO,
  output full
);

  wire clock_1_out, clock_2_out;
  wire [5:0] adder_1_out, register_1_q;

  Clock clock_1 (.out(clock_1_out));
  Register #(.width(6)) register_1 (.D(adder_1_out), .en(wO), .clk(clock_1_out), .Q(register_1_q));  // open: clr
  Adder #(.width(6)) adder_1 (.a(register_1_q), .b(6'b000001), .out(adder_1_out));  // open: cin, cout
  // RAM #(.addrWidth(6)) ram_1: pin names not known; wires that end beside it: register_1_q, DOUT
  Clock clock_2 (.out(clock_2_out));
  Comparator #(.width(6), .mode("unsigned")) comparator_1 (.a(register_1_q), .b({6{1'b1}}), .eq(full));  // open: gt, lt

  // Notes on the sheet:
  //   contents of ram_1 (hex, n*v repeats v):
  //   f1 f0
endmodule

module tmp (
  input  in_1,
  input  in_2,
  input  [1:0] muxR,
  input  in_4,
  input  in_5,
  input  in_6,
  input  in_7,
  input  in_8,
  input  ijump,
  input  [2:0] aluCtl,
  input  in_11,
  input  in_12,
  input  wPC,
  input  [2:0] in_14,
  input  wO,
  output [3:0] out_16
);

  wire clock_1_out;

  Clock clock_1 (.out(clock_1_out));
  // FSM_Entity #(.content("fsm example @[ 50 , 50 , 800 , 500 ]\n{ in A [ 3 ] @[ 50 , 100 , 44 , 15 ]\n;\nout X [ 4 ] @[ 807 , 140 , 43 , 15 ]\n;\ncodeWidth = 2 ; reset = S0 ; state S0 = \"00\" @[ 249 , 171 , 30 , 30 ]\n{\ncommands @[ 294 , 186 , 67 , 21 ]\n{\nX = \"0001\" ;\n}\ntransitions {\nS0 -> S1 when default @[ 372 , 148 , 50 , 21 ]\n;\nS0 -> S3 when A == \"000\" @[ 346 , 269 , 78 , 21 ]\n;\n}\n}\nstate S1 = \"10\" @[ 467 , 146 , 30 , 30 ]\n{\ncommands @[ 512 , 161 , 67 , 21 ]\n{\nX = \"0010\" ;\n}\ntransitions {\nS1 -> S2 when default @[ 533 , 276 , 50 , 21 ]\n;\nS1 -> S0 when A == \"000\" @[ 376 , 216 , 78 , 21 ]\n;\n}\n}\nstate S2 = \"00\" @[ 471 , 339 , 30 , 30 ]\n{\ncommands @[ 543 , 353 , 131 , 21 ]\n{\nX = { \"00\" , A [ 1 : 0 ] , \"1\" } ;\n}\ntransitions {\nS2 -> S3 when default @[ 392 , 398 , 50 , 21 ]\n;\nS2 -> S1 when A [ 2 : 1 ] == \"11\" @[ 557 , 250 , 100 , 21 ]\n;\n}\n}\nstate S3 = \"10\" @[ 265 , 329 , 30 , 30 ]\n{\ncommands @[ 310 , 344 , 67 , 21 ]\n{\nX = \"1000\" ;\n}\ntransitions {\nS3 -> S0 when default @[ 248 , 278 , 50 , 21 ]\n;\nS3 -> S2 when A == \"000\" @[ 388 , 313 , 78 , 21 ]\n;\n}\n}\n}")) fsm_entity_1: pin names not known; wires that end beside it: clock_1_out, in_11, in_12, in_14, out_16

  // Other names for the same wires on the sheet: branch = in_8; muxM = in_4; rIN = in_2; srcA = in_5; wIR = in_1;
  //   wM = in_7; wR = in_6
endmodule
